// Logisim project Display-7-Seg.circ as structural Verilog: 1 circuit, main circuit main
module main (
  input  A,
  input  B,
  input  C,
  input  D
);

  wire A_out, and_1_out, and_2_out, and_3_out, and_4_out, and_5_out, and_6_out, and_7_out, and_8_out,
       and_9_out, and_10_out, and_11_out, and_12_out, and_13_out, and_14_out, B_out, C_out, D_out, E_out,
       F_out, G_out, not_1_out, not_2_out, not_3_out, not_4_out, or_1_out;

  not not_1 (not_1_out, A);
  not not_2 (not_2_out, C);
  not not_3 (not_3_out, B);
  not not_4 (not_4_out, D);
  and and_1 (and_1_out, B, D);
  and and_2 (and_2_out, not_3_out, not_4_out);
  and and_3 (and_3_out, not_2_out, not_4_out);
  and and_4 (and_4_out, C, D);
  and and_5 (and_5_out, not_3_out, not_4_out);
  and and_6 (and_6_out, C, not_4_out);
  or or_1 (or_1_out, not_3_out, C);
  and and_7 (and_7_out, not_2_out, not_4_out);
  and and_8 (and_8_out, B, not_2_out);
  and and_9 (and_9_out, B, not_4_out);
  and and_10 (and_10_out, B, not_2_out);
  and and_11 (and_11_out, B, not_4_out);
  and and_12 (and_12_out, not_3_out, C);
  or u_A (A_out, A, C, and_1_out, and_2_out);
  or u_B (B_out, not_3_out, and_3_out, and_4_out);
  or u_C (C_out, B, not_2_out, D);
  and and_13 (and_13_out, not_3_out, C);
  and E (E_out, not_4_out, or_1_out);
  or F (F_out, A, and_7_out, and_8_out, and_9_out);
  or G (G_out, A, and_10_out, and_11_out, and_12_out);
  or u_D (D_out, A, and_13_out, and_14_out, and_5_out, and_6_out);
  and and_14 (and_14_out, B, not_2_out, D);
  _7_Segment_Display u_7_segment_display_1 (
    .g(G_out), .f(F_out), .a(A_out), .b(B_out), .e(E_out), .d(D_out), .c(C_out));  // open: dp

  // Notes on the sheet:
  //   Alunos: Bianca Borges e Hsi Jia Hao
  //   Professor: Ramon Bezerra
endmodule
