// Logisim project Display7seg.circ as structural Verilog: 1 circuit, main circuit main
module main (
  input  [3:0] in_1
);

  wire and_1_out, and_2_out, and_3_out, and_4_out, and_5_out, and_6_out, and_7_out, and_8_out, and_9_out,
       and_10_out, and_11_out, and_12_out, and_13_out, button_1_out, clock_1_out, comparator_1_eq, nor_1_out,
       not_1_out, not_2_out, not_3_out, not_5_out, or_1_out, or_2_out, or_3_out, or_4_out, or_5_out,
       or_6_out, or_7_out, s_r_ff_1_q, xnor_1_out, xnor_2_out;
  wire [3:0] counter_1_q;

  Clock clock_1 (.out(clock_1_out));
  nor nor_1 (nor_1_out, counter_1_q[0], counter_1_q[2], counter_1_q[1], counter_1_q[3]);
  and and_1 (and_1_out, counter_1_q[0], counter_1_q[3]);
  S_R_Flip_Flop s_r_ff_1 (.Q(s_r_ff_1_q), .reset(and_1_out), .preset(nor_1_out));  // open: S, R, clk, Qn
  not not_1 (not_1_out, counter_1_q[0]);
  not not_2 (not_2_out, counter_1_q[1]);
  not not_3 (not_3_out, counter_1_q[2]);
  // NOT_Gate not_4 has open pins: in=counter_1_q[3], out=open
  and and_2 (and_2_out, clock_1_out, not_5_out);
  xnor xnor_1 (xnor_1_out, counter_1_q[2], counter_1_q[0]);
  xnor xnor_2 (xnor_2_out, counter_1_q[1], counter_1_q[0]);
  and and_3 (and_3_out, not_3_out, not_1_out);
  and and_4 (and_4_out, not_3_out, counter_1_q[1]);
  and and_5 (and_5_out, counter_1_q[1], not_1_out);
  and and_6 (and_6_out, counter_1_q[2], not_2_out, counter_1_q[0]);
  or or_1 (or_1_out, not_3_out, counter_1_q[1]);
  and and_7 (and_7_out, not_2_out, not_1_out);
  and and_8 (and_8_out, counter_1_q[2], not_2_out);
  and and_9 (and_9_out, counter_1_q[2], not_1_out);
  and and_10 (and_10_out, counter_1_q[2], not_2_out);
  and and_11 (and_11_out, not_3_out, counter_1_q[1]);
  and and_12 (and_12_out, counter_1_q[1], not_1_out);
  Counter #(.max('hf), .width(4)) counter_1 (
    .Q(counter_1_q), .up(s_r_ff_1_q), .clk(and_2_out), .clr(button_1_out));  // open: load, D, count, carry
  or or_2 (or_2_out, counter_1_q[3], counter_1_q[1], xnor_1_out);
  or or_3 (or_3_out, not_3_out, xnor_2_out);
  or or_4 (or_4_out, counter_1_q[2], not_2_out, counter_1_q[0]);
  or or_5 (or_5_out, counter_1_q[3], and_3_out, and_4_out, and_5_out, and_6_out);
  and and_13 (and_13_out, not_1_out, or_1_out);
  or or_6 (or_6_out, counter_1_q[3], and_7_out, and_8_out, and_9_out);
  or or_7 (or_7_out, counter_1_q[3], and_10_out, and_11_out, and_12_out);
  not not_5 (not_5_out, comparator_1_eq);
  Comparator #(.width(4)) comparator_1 (.a(counter_1_q), .b(in_1), .eq(comparator_1_eq));  // open: gt, lt
  Button button_1 (.out(button_1_out));
  _7_Segment_Display u_7_segment_display_1 (
    .g(or_7_out), .f(or_6_out), .a(or_2_out), .b(or_3_out), .e(and_13_out), .d(or_5_out), .c(or_4_out));  // open: dp
endmodule
